# Fritzing sketch SensorPump (saved by Fritzing 0.9.4)
circuit board: 24.17cm x 15.8156cm
breadboards: 1

parts:
  U1 = LCD-16X2 [package=lcd-16x2_noholes]
  R1_(4_7-10) = Resistor [tolerance=±5% resistance=4.7k package=THT]
  MOSF = IFR520 MOS module [package=THT]
  Pump = DC Motor
  Power_5v_1A = USB_MICROB_PLUG [package=micro-b-th]
  Humidity_sensor = Soil Moisture Sensor
  LCM1602_IIC1 = LCM1602 IIC [part_number="LCM1602 IIC" chip_label="LCM1602 IIC" package="DIP (Dual Inline) [THT]"]
  Компонент1 = Arduino Nano (Rev3.0)
  DS1 = DS18B20 1-Wire Temperature Sensor [part_number=DS18B20]

nets:
  VSS: U1.VSS, LCM1602_IIC1.VSS
  VDD: U1.VDD, LCM1602_IIC1.VDD
  N1: U1.VO, LCM1602_IIC1.V0
  N2: U1.RS, LCM1602_IIC1.RS
  N3: U1.R_W, LCM1602_IIC1.RW
  N4: U1.E, LCM1602_IIC1.E
  N5: U1.DB0, LCM1602_IIC1.D0
  N6: U1.DB1, LCM1602_IIC1.D1
  N7: U1.DB2, LCM1602_IIC1.D2
  N8: U1.DB3, LCM1602_IIC1.D3
  N9: U1.DB4, LCM1602_IIC1.D4
  N10: U1.DB5, LCM1602_IIC1.D5
  N11: U1.DB6, LCM1602_IIC1.D6
  N12: U1.DB7, LCM1602_IIC1.D7
  N13: U1.A, LCM1602_IIC1.A
  N14: U1.K, LCM1602_IIC1.K
  N15: R1_(4_7-10).Pin_0, Компонент1.A1, DS1.DQ
  VCC: R1_(4_7-10).Pin_1, MOSF.VIN, Power_5v_1A.VCC, Humidity_sensor.VCC, LCM1602_IIC1.VCC, Компонент1.5V, DS1.VDD
  N16: MOSF.SIG, Компонент1.D3
  GND: MOSF.GND, Power_5v_1A.GND, Humidity_sensor.GND, DS1.GND
  N17: MOSF.V+, Pump.pin_1
  N18: MOSF.V-, Pump.pin_2
  N19: Humidity_sensor.SIG, Компонент1.A2
  GND_2: LCM1602_IIC1.GND, Компонент1.GND
  N20: LCM1602_IIC1.SDA, Компонент1.A4
  N21: LCM1602_IIC1.SCL, Компонент1.A5

custom parts:
  LCM1602 IIC: I2C-Module to use a 1602 or 2004 LCD on with the wire.h libory Serial LCD Modul

// code stored in the sketch: SensorPump.ino
// НАСТРОЙКА ПИНОВ
#define PinDs A1      // Пин подключения датчика температуры DS18B20
#define PinHum A2     // Пин подключения датчика влажности
#define MosPump 3     // Пин подключения мосфета для контроля помпы

// НАСТРОЙКИ РАБОТЫ СИСТЕМЫ АВТОПОЛИВА
#define Hum_min 30          // Нижний предел влажности почвы в процентах (когда нужно включать)
#define Hum_max 50          // Верхний предел влажности почвы в процентах (когда нужно выключать)

#define AnalogMin 650       // Показания датчика влажности в сухой почве
#define AnalogMax 300       // Показания датчика влажности в воде

#include <LiquidCrystal_I2C.h>    // Подключение библиотеки для работы с дисплеем
byte degree[8]   = {B11100,B10100,B11100,B00000,B00000,B00000,B00000,B00000,};    // Попиксельная прорисовка символа градуса
LiquidCrystal_I2C lcd(0x27,16,2);   // Задаем адрес и размер дисплея

#include <microDS18B20.h>   // Подключение библиотеки для работы с датчиком температуры
MicroDS18B20 dallasSensors(PinDs);    // Инициализация датчика


// ОБЪЯВЛЕНИЕ ПЕРЕМЕННЫХ
unsigned long readTimer;
uint16_t hum;
float temp;
 
void setup()
{
  delay(300);                   // Ждём готовности модулей 300мс перед началом инициализации
  Serial.begin(9600);           // Устанавливаем скорость передачи данных с модулей в 9600 бод   
                    
  lcd.init();                   // Инициализация дисплея    
  lcd.createChar(1, degree);    // Создаем символ градуса и присваиваем ему номер 1
  lcd.backlight();              // Включение подсветки дисплея 

  pinMode(MosPump, OUTPUT);     // Настройка пинов подключения мосфетов на вывод                
}


void loop()
{
  if (millis() - readTimer > 1000) {  // Секундный таймер (для стабильности измерений) (millis() считает время с момента включения программы, при превышении разницы значений запуск условия)
    
    temp = dallasSensors.getTemp();   // Считывание показаний датчика температуры DS18B20
    dallasSensors.requestTemp();

    hum = analogRead(PinHum);             // Считывание показаний влажности
    hum = map(hum, AnalogMin, AnalogMax, 0, 100);     // Нормализация значений влажности

            // ОТЛАДКА (вывод в монитор порта)
            Serial.print("\t"); 
            Serial.print(String(temp));
            Serial.print("\t");
            Serial.print(String(hum));
            Serial.print("\t");
            Serial.println("MosPump_" + String(digitalRead(MosPump)));

    readTimer = millis();                 // Обнулить таймер (делаем разность значений равной нулю)
  }

    // Условия работы помпы                        
    if (hum < Hum_min) {                                                        
      digitalWrite(MosPump, LOW);    // Включение мосфета помпы (ВНИМАНИЕ! Замени LOW на HIGH, чтобы помпа начала включаться)
      lcd.setCursor(11,1);
      lcd.print(" (ON)");
    }                                
    if (hum > Hum_max) {                                          
      digitalWrite(MosPump, LOW);     // Выключение мосфета помпы  
      lcd.setCursor(11,1);
      lcd.print("(OFF)");         
    }   
              
  lcd.setCursor(0,0);           // Устанавливаем курсор на 1 строку, ячейка 1
  lcd.print("TEMP = " + String(temp) + "\1C ");      // Выводим показания температуры и символ градуса
  
  lcd.setCursor(0,1);           // Устанавливаем курсор на 2 строку, ячейка 1
  lcd.print("HUM = " + String(hum) + "%  ");       // Выводим показания влажности              
 
  delay(5);                     // Задержка выполнения тела программы для стабильности работы
}
