# Fritzing sketch Incubator (saved by Fritzing 0.9.4)
breadboards: 1

parts:
  U1 = LCD-16X2 [package=lcd-16x2_noholes]
  Компонент1 = Arduino Nano (Rev3.0)
  LCM1602_IIC1 = LCM1602 IIC [part_number="LCM1602 IIC" chip_label="LCM1602 IIC" package="DIP (Dual Inline) [THT]"]
  ZS-042_RTC1 = ZS-042 RTC Module
  Encoder1 = AMT103
  DHT1 = DHT11 Humitidy and Temperature Sensor
  DS1 = DS18B20 1-Wire Temperature Sensor [part_number=DS18B20]
  Hall_Sensor = HALL-EFFECT [package=sc70]
  Power_12v_5A = Power Jack [package=power_jack_slot]
  R1_(4_7-10) = Resistor [tolerance=±5% resistance=4.7k package=THT]
  12v_to_5v_for_sensors = RioRand LM2596

nets:
  VSS: U1.VSS, LCM1602_IIC1.VSS
  VDD: U1.VDD, LCM1602_IIC1.VDD
  N1: U1.VO, LCM1602_IIC1.V0
  N2: U1.RS, LCM1602_IIC1.RS
  N3: U1.R_W, LCM1602_IIC1.RW
  N4: U1.E, LCM1602_IIC1.E
  N5: U1.DB0, LCM1602_IIC1.D0
  N6: U1.DB1, LCM1602_IIC1.D1
  N7: U1.DB2, LCM1602_IIC1.D2
  N8: U1.DB3, LCM1602_IIC1.D3
  N9: U1.DB4, LCM1602_IIC1.D4
  N10: U1.DB5, LCM1602_IIC1.D5
  N11: U1.DB6, LCM1602_IIC1.D6
  N12: U1.DB7, LCM1602_IIC1.D7
  N13: U1.A, LCM1602_IIC1.A
  N14: U1.K, LCM1602_IIC1.K
  N15: Компонент1.D0/RX, Encoder1.X
  N16: Компонент1.D2, Encoder1.B
  N17: Компонент1.D3, Encoder1.A
  GND: Компонент1.GND, LCM1602_IIC1.GND, ZS-042_RTC1.GND, Encoder1.GND, DHT1.GND, DS1.GND, Hall_Sensor.GND, 12v_to_5v_for_sensors.Pin_4
  VCC: Компонент1.5V, LCM1602_IIC1.VCC, ZS-042_RTC1.VCC, Encoder1.5V, DHT1.VDD, DS1.VDD, Hall_Sensor.VCC, R1_(4_7-10).Pin_1, 12v_to_5v_for_sensors.Pin_3
  N18: Компонент1.A6, Hall_Sensor.OUT
  N19: Компонент1.A5, LCM1602_IIC1.SCL, ZS-042_RTC1.SCL
  N20: Компонент1.A4, LCM1602_IIC1.SDA, ZS-042_RTC1.SDA
  N21: Компонент1.A3, DHT1.DATA
  N22: Компонент1.A2, DS1.DQ, R1_(4_7-10).Pin_0
  N23: Power_12v_5A.GND, 12v_to_5v_for_sensors.Pin_2
  N24: Power_12v_5A.PWR, 12v_to_5v_for_sensors.Pin_1

custom parts:
  LCM1602 IIC: I2C-Module to use a 1602 or 2004 LCD on with the wire.h libory Serial LCD Modul
  DHT11 Humitidy and Temperature Sensor: DHT11 Humidity and Temperature Sensor
