# Fritzing sketch SmartLamp (saved by Fritzing 0.9.4)
circuit board: 21.9143cm x 12.1775cm
breadboards: 1

parts:
  Arduino_Nano = Arduino Nano (Rev3.0)
  Touch = TTP223 Touch Module [part_number=TTP223]
  RGB_LED = ws2812b [package="smd 2812b"]
  220 = Resistor [tolerance=±5% resistance=220 package=THT]
  Sensor_H/P/T = Adafruit BME280
  RTC_DS3231 = ZS-042 RTC Module
  Encoder = AMT103
  Компонент1 = Bluetooth Mate Silver  # not connected
  Power_5v = Power Jack [package=power_jack_smd]
  LCM1602_IIC2 = LCM1602 IIC [part_number="LCM1602 IIC" chip_label="LCM1602 IIC" package="DIP (Dual Inline) [THT]"]
  U2 = LCD-16X2 [package=lcd-16x2_noholes]

nets:
  GND: Arduino_Nano.GND, Touch.GND, RGB_LED.VSS, Sensor_H/P/T.GND, RTC_DS3231.GND, Encoder.GND, Power_5v.GND, LCM1602_IIC2.GND
  N1: Arduino_Nano.D2, Touch.I/O
  N2: Arduino_Nano.D3, 220.Pin_1
  N3: Arduino_Nano.D8, Encoder.B
  N4: Arduino_Nano.D9, Encoder.A
  N5: Arduino_Nano.D10, Encoder.X
  VCC: Arduino_Nano.5V, Touch.VCC, RGB_LED.VDD, RTC_DS3231.VCC, Encoder.5V, Power_5v.PWR, LCM1602_IIC2.VCC
  N6: Arduino_Nano.A5, Sensor_H/P/T.SCK/SCL, RTC_DS3231.SCL, LCM1602_IIC2.SCL
  N7: Arduino_Nano.A4, Sensor_H/P/T.SDI/SDA, RTC_DS3231.SDA, LCM1602_IIC2.SDA
  3V3: Arduino_Nano.3V3, Sensor_H/P/T.3.3V
  N8: RGB_LED.DIN, 220.Pin_0
  VSS: LCM1602_IIC2.VSS, U2.VSS
  VDD: LCM1602_IIC2.VDD, U2.VDD
  N9: LCM1602_IIC2.V0, U2.VO
  N10: LCM1602_IIC2.RS, U2.RS
  N11: LCM1602_IIC2.RW, U2.R_W
  N12: LCM1602_IIC2.E, U2.E
  N13: LCM1602_IIC2.D0, U2.DB0
  N14: LCM1602_IIC2.D1, U2.DB1
  N15: LCM1602_IIC2.D2, U2.DB2
  N16: LCM1602_IIC2.D3, U2.DB3
  N17: LCM1602_IIC2.D4, U2.DB4
  N18: LCM1602_IIC2.D5, U2.DB5
  N19: LCM1602_IIC2.D6, U2.DB6
  N20: LCM1602_IIC2.D7, U2.DB7
  N21: LCM1602_IIC2.A, U2.A
  N22: LCM1602_IIC2.K, U2.K

custom parts:
  TTP223 Touch Module: Single touch module. Other side has "A" "B" terminal to short and use "AHLB" & "Toggle" Mode.
  Adafruit BME280: Bosch has stepped up their game with their new BME280 sensor, an environmental sensor with temperature, barometric pressure and humidity! This sensor is great for all sorts of weather/environmental sensing and can even be used in both I2C and SPI! This precision sensor from Bosch is the best low-cost sensing solution for measuring humidity with ±3% accuracy, barometric pressure with ±1 hPa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
  LCM1602 IIC: I2C-Module to use a 1602 or 2004 LCD on with the wire.h libory Serial LCD Modul
